# Fritzing sketch hot wire (saved by Fritzing 0.9.3b)
circuit board: 5.30962cm x 7.01053cm
circuit board: 10.525cm x 1.83062cm
breadboards: 1

parts:
  HEF1 = HEF4094 [package="DIP16 [THT]"]
  R2 = Resistor [tolerance=±5% resistance=220 package=THT]
  R3 = Resistor [tolerance=±5% resistance=220 package=THT]
  R1 = Resistor [tolerance=±5% resistance=220 package=THT]
  R5 = Resistor [tolerance=±5% resistance=220 package=THT]
  R6 = Resistor [tolerance=±5% resistance=220 package=THT]
  R7 = Resistor [tolerance=±5% resistance=220 package=THT]
  R8 = Resistor [tolerance=±5% resistance=220 package=THT]
  Level_Select = Hexadecimal Rotary Encoder [part_number=APEM-PT65-303 package=THT]
  Start = Pushbutton [package="[THT]"]
  LED9_(Alarm) = smd LED [color="Red (633nm)" package="1206 [SMD]"]
  R9 = Resistor [tolerance=±5% resistance=220 package=THT]
  R10 = Resistor [tolerance=±5% resistance=10k package=THT]
  R11 = Resistor [tolerance=±5% resistance=10k package=THT]
  R12 = Resistor [tolerance=±5% resistance=10k package=THT]
  R13 = Resistor [tolerance=±5% resistance=1k package=THT]
  C1 = Electrolytic Capacitor [capacitance=100nF package="100 mil [THT, electrolytic]"]
  M1 = DC Motor
  D1 = Rectifier Diode [part_number=1N4001 package="300 mil [THT]"]
  Q1 = NPN-Transistor [package="TO92 [THT]"]
  J4 = male pin header, 7 pins [form="♂ (male)"]
  J1 = female pin header, 7 pins [form="♀ (female)"]
  Loop = Inductor [package="400 mil [THT]"]
  L2 = Inductor [package="400 mil [THT]"]
  L3 = Inductor [package="400 mil [THT]"]
  L4 = Inductor [package="400 mil [THT]"]
  Bauteil2 = Arduino Uno (Rev3)
  R4 = Resistor [tolerance=±5% resistance=220 package=THT]
  LED1 = LED - 3mm [color="Red (633nm)" package="3 mm [THT]"]
  LED2 = LED - 3mm [color="Red (633nm)" package="3 mm [THT]"]
  LED3 = LED - 3mm [color="Yellow (585nm)" package="3 mm [THT]"]
  LED4 = LED - 3mm [color="Yellow (585nm)" package="3 mm [THT]"]
  LED5 = LED - 3mm [color="Yellow (592nm)" package="3 mm [THT]"]
  LED6 = LED - 3mm [color="Green (560nm)" package="3 mm [THT]"]
  LED7 = LED - 3mm [color="Green (560nm)" package="3 mm [THT]"]
  LED8 = LED - 3mm [color="Green (560nm)" package="3 mm [THT]"]
  SPKR1 = Loudspeaker
  R14 = Resistor [tolerance=±5% resistance=220 package=THT]
  R15 = Resistor [tolerance=±5% resistance=10k package=THT]

nets:
  N1: HEF1.STROBE, Bauteil2.D5_PWM
  N2: HEF1.DATA, Bauteil2.D6_PWM
  N3: HEF1.CLOCK, Bauteil2.D7
  N4: HEF1.Q1, R8.Pin_1
  N5: HEF1.Q2, R7.Pin_1
  N6: HEF1.Q3, R6.Pin_1
  N7: HEF1.Q4, R5.Pin_1
  VSS: HEF1.Vss, R9.Pin_0, R10.Pin_0, R11.Pin_0, R12.Pin_0, Bauteil2.GND, LED1.cathode, LED2.cathode, LED3.cathode, LED4.cathode, LED5.cathode, LED6.cathode, LED7.cathode, LED8.cathode, SPKR1.pin1, R15.Pin_0
  N8: HEF1.Q8, R1.Pin_0
  N9: HEF1.Q7, R2.Pin_0
  N10: HEF1.Q6, R3.Pin_0
  N11: HEF1.Q5, R4.Pin_0
  VDD: HEF1.OE, HEF1.Vdd, Level_Select.InputCommon, Level_Select.InputCommon2, Start.Pin_1, Start.Pin_2, C1.-, D1.cathode, Q1.C, J4.pin4, Bauteil2.5V
  N12: R2.Pin_1, LED2.anode
  N13: R3.Pin_1, LED3.anode
  N14: R1.Pin_1, LED1.anode
  N15: R5.Pin_0, LED5.anode
  N16: R6.Pin_0, LED6.anode
  N17: R7.Pin_0, LED7.anode
  N18: R8.Pin_0, LED8.anode
  N19: Level_Select.Output1Pin, Bauteil2.D3_PWM
  N20: Level_Select.Output2Pin, Bauteil2.D1/TX
  N21: Level_Select.Output4Pin, Bauteil2.D2
  N22: Level_Select.Output8pin, Bauteil2.D0/RX
  N23: Start.Pin_3, Start.Pin_4, Bauteil2.A5/SCL, R15.Pin_1
  N24: LED9_(Alarm).cathode, J1.pin2
  N25: LED9_(Alarm).anode, J1.pin1
  N26: R9.Pin_1, J4.pin1
  N27: R10.Pin_1, J4.pin5, Bauteil2.A2
  N28: R11.Pin_1, J4.pin6, Bauteil2.A1
  N29: R12.Pin_1, J4.pin7, Bauteil2.A0
  N30: R13.Pin_0, Q1.B
  N31: R13.Pin_1, Bauteil2.D13/SCK
  N32: C1.+, D1.anode, Q1.E, J4.pin3
  N33: M1.pin_1, J1.pin3
  N34: M1.pin_2, J1.pin4, Loop.pin_0
  N35: J4.pin2, Bauteil2.D12/MISO
  N36: J1.pin5, L2.pin_1
  N37: J1.pin6, L3.pin_1
  N38: J1.pin7, L4.pin_1
  N39: Bauteil2.D11_PWM/MOSI, R14.Pin_1
  N40: R4.Pin_1, LED4.anode
  N41: SPKR1.pin2, R14.Pin_0
